// Logisim project part1.circ as structural Verilog: 7 circuits, main circuit main
module main (
  input  in_1,
  input  in_2,
  output out_3
);

  NAND nand_1 (.in_1(in_1), .in_2(in_2), .out_3(out_3));
endmodule

module NAND (
  input  in_1,
  input  in_2,
  output out_3
);

  wire and_1_out;

  and and_1 (and_1_out, in_1, in_2);
  not not_1 (out_3, and_1_out);
endmodule

module NOR (
  input  in_1,
  input  in_2,
  output out_3
);

  or or_1 (out_3, in_1, in_2);
endmodule

module XOR (
  input  in_1,
  input  in_2,
  output out_3
);

  wire and_1_out, not_1_out, or_1_out;

  and and_1 (and_1_out, in_1, in_2);
  or or_1 (or_1_out, in_1, in_2);
  not not_1 (not_1_out, and_1_out);
  and and_2 (out_3, not_1_out, or_1_out);
endmodule

module _2to1Mux (
  input  in_1,
  input  in_2,
  input  in_3,
  output out_4
);

  wire and_1_out, and_2_out, not_1_out;

  and and_1 (and_1_out, in_1, not_1_out);
  not not_1 (not_1_out, in_3);
  and and_2 (and_2_out, in_3, in_2);
  or or_1 (out_4, and_1_out, and_2_out);
endmodule

module _4to1Mux (
  input  in_1,
  input  in_2,
  input  in_3,
  input  in_4,
  input  in_5,
  input  in_6,
  output out_7
);

  wire and_1_out, and_2_out, and_3_out, and_4_out, n4decoder_1_out_3, n4decoder_1_out_4, n4decoder_1_out_5,
       n4decoder_1_out_6;

  _4decoder u_4decoder_1 (
    .in_1(in_5), .in_2(in_6), .out_3(n4decoder_1_out_3), .out_4(n4decoder_1_out_4),
    .out_5(n4decoder_1_out_5), .out_6(n4decoder_1_out_6));
  and and_1 (and_1_out, in_1, n4decoder_1_out_3);
  and and_2 (and_2_out, in_2, n4decoder_1_out_4);
  and and_3 (and_3_out, in_3, n4decoder_1_out_5);
  and and_4 (and_4_out, in_4, n4decoder_1_out_6);
  or or_1 (out_7, and_1_out, and_2_out, and_3_out, and_4_out);
endmodule

module _4decoder (
  input  in_1,
  input  in_2,
  output out_3,
  output out_4,
  output out_5,
  output out_6
);

  wire not_1_out, not_2_out, not_3_out, not_4_out;

  not not_1 (not_1_out, in_1);
  not not_2 (not_2_out, in_2);
  not not_3 (not_3_out, in_1);
  not not_4 (not_4_out, in_2);
  and and_1 (out_3, not_1_out, not_2_out);
  and and_2 (out_4, not_3_out, in_2);
  and and_3 (out_5, in_1, not_4_out);
  and and_4 (out_6, in_1, in_2);
endmodule
