// Logisim project lab06.circ as structural Verilog: 6 circuits, main circuit main
module main (
  input  [3:0] in_1,
  input  [15:0] in_2,
  output [15:0] out_3
);

  wire [15:0] rotr1_1_out_3, rotr2_1_out_3, rotr3_1_out_3;

  rotr1 rotr1_1 (.\input (in_2), .select(in_1[0]), .out_3(rotr1_1_out_3));
  rotr2 rotr2_1 (.in_2(rotr1_1_out_3), .in_1(in_1[1]), .out_3(rotr2_1_out_3));
  rotr3 rotr3_1 (.in_2(rotr2_1_out_3), .in_1(in_1[2]), .out_3(rotr3_1_out_3));
  rotr4 rotr4_1 (.in_2(rotr3_1_out_3), .in_1(in_1[3]), .out_3(out_3));
endmodule

module Ex1 (
  input  [7:0] Input,
  output Out1,
  output [7:0] Out2
);

  not not_1 (Out2[7], Input[7]);
  and and_1 (Out1, Input[0], Input[7]);

  assign Out2[6:0] = Input[6:0];
endmodule

module rotr1 (
  input  select,
  input  [15:0] \input ,
  output [15:0] out_3
);

  Multiplexer #(.width(16), .enable("false")) multiplexer_1 (
    .in0(\input ), .in1({\input [0], \input [15:1]}), .out(out_3), .sel(select));
endmodule

module rotr2 (
  input  in_1,
  input  [15:0] in_2,
  output [15:0] out_3
);

  Multiplexer #(.width(16), .enable("false")) multiplexer_1 (
    .in0(in_2), .in1({in_2[0], in_2[1], in_2[15:2]}), .out(out_3), .sel(in_1));
endmodule

module rotr3 (
  input  in_1,
  input  [15:0] in_2,
  output [15:0] out_3
);

  wire [15:0] rotr2_1_out_3;

  rotr2 rotr2_1 (.in_2(in_2), .in_1(in_1), .out_3(rotr2_1_out_3));
  rotr2 rotr2_2 (.in_2(rotr2_1_out_3), .in_1(in_1), .out_3(out_3));
endmodule

module rotr4 (
  input  in_1,
  input  [15:0] in_2,
  output [15:0] out_3
);

  wire [15:0] rotr3_1_out_3;

  rotr3 rotr3_1 (.in_2(in_2), .in_1(in_1), .out_3(rotr3_1_out_3));
  rotr3 rotr3_2 (.in_2(rotr3_1_out_3), .in_1(in_1), .out_3(out_3));
endmodule
